# Fritzing sketch pcb-had (saved by Fritzing 0.9.2b)
circuit board: 4.95cm x 4.95cm
breadboards: 1

parts:
  ankle = mystery part, 3 pins [chip_label=?]
  knee = mystery part, 3 pins [chip_label=?]
  hip = mystery part, 3 pins [chip_label=?]
  hip_2 = mystery part, 3 pins [chip_label=?]
  knee_2 = mystery part, 3 pins [chip_label=?]
  ankle_2 = mystery part, 3 pins [chip_label=?]
  ankle_3 = mystery part, 3 pins [chip_label=?]
  knee_3 = mystery part, 3 pins [chip_label=?]
  hip_3 = mystery part, 3 pins [chip_label=?]
  hip_4 = mystery part, 3 pins [chip_label=?]
  ankle_4 = mystery part, 3 pins [chip_label=?]
  knee_4 = mystery part, 3 pins [chip_label=?]
  +bat- = mystery part, 2 pins [chip_label=?]
  10kΩ = Resistor [tolerance=±5% resistance=220 package="0805 [SMD]"]
  R2 = Resistor [tolerance=±5% resistance=220 package="0805 [SMD]"]
  U13 = mystery part, 3 pins [chip_label=?]
  U14 = mystery part, 3 pins [chip_label=?]
  U15 = mystery part, 3 pins [chip_label=?]
  U16 = mystery part, 3 pins [chip_label=?]
  U17 = mystery part, 3 pins [chip_label=?]
  U18 = mystery part, 3 pins [chip_label=?]
  U19 = mystery part, 3 pins [chip_label=?]
  U20 = mystery part, 3 pins [chip_label=?]
  Pad1 = Pad [width=2.54 height=5.08 connect=center]
  on = Pad [width=2.54 height=5.08 connect=center]
  off = Pad [width=2.54 height=5.08 connect=center]  # not connected
  esp-01 = mystery part, 8 pins [chip_label=?]
  10kΩ_2 = Resistor [tolerance=±5% resistance=220 package="0805 [SMD]"]
  R4 = Resistor [tolerance=±5% resistance=220 package="0805 [SMD]"]
  10kΩ_3 = Resistor [tolerance=±5% resistance=220 package="0805 [SMD]"]
  J1 = double row female pin header, 6 pins [form="♀ (female)"]
  J2 = female pin header, 12 pins [form="♀ (female)"]
  J3 = female pin header, 12 pins [form="♀ (female)"]
  J4 = female pin header, 2 pins [form="♀ (female)"]
  1000µF = Electrolytic Capacitor [capacitance=1µF package="100 mil [THT, electrolytic]"]
  J5 = female pin header, 2 pins [form="♀ (female)"]
  scl_sda_gnd = mystery part, 3 pins [chip_label=?]
  rx_tx_gnd = mystery part, 3 pins [chip_label=?]

nets:
  N1: ankle.pin1, knee.pin1, hip.pin1, hip_2.pin1, knee_2.pin1, ankle_2.pin1, U13.pin1, U14.pin1, U15.pin1, U16.pin1, U17.pin1, U18.pin1, U19.pin1, U20.pin1, J3.pin2, 1000µF.-, scl_sda_gnd.pin1
  N2: ankle.pin2, knee.pin2, hip.pin2, hip_2.pin2, knee_2.pin2, ankle_2.pin2, ankle_3.pin2, knee_3.pin2, hip_3.pin2, hip_4.pin2, ankle_4.pin2, knee_4.pin2, Pad1.pad, esp-01.pin5, 10kΩ_2.Pin_0, R4.Pin_0, J1.pin1, J1.pin2, J3.pin1, 1000µF.+
  N3: ankle.pin3, J3.pin12
  N4: knee.pin3, J3.pin11
  N5: hip.pin3, J3.pin10
  N6: hip_2.pin3, J3.pin8
  N7: knee_2.pin3, J3.pin7
  N8: ankle_2.pin3, J3.pin6
  N9: ankle_3.pin1, knee_3.pin1, hip_3.pin1, hip_4.pin1, ankle_4.pin1, knee_4.pin1, +bat-.pin1, esp-01.pin1, 10kΩ_3.Pin_0, J1.pin3, J2.pin4, rx_tx_gnd.pin1
  N10: ankle_3.pin3, J2.pin12
  N11: knee_3.pin3, J2.pin11
  N12: hip_3.pin3, J2.pin10
  N13: hip_4.pin3, J2.pin9
  N14: ankle_4.pin3, J2.pin7
  N15: knee_4.pin3, J2.pin8
  N16: +bat-.pin2, on.pad
  N17: 10kΩ.Pin_0, esp-01.pin2, J1.pin5, J4.pin1, scl_sda_gnd.pin3
  N18: 10kΩ.Pin_1, R2.Pin_1, U13.pin2, U14.pin2, U15.pin2, U16.pin2, U17.pin2, U18.pin2, U19.pin2, U20.pin2, J3.pin4
  N19: R2.Pin_0, esp-01.pin3, J1.pin4, J4.pin2, scl_sda_gnd.pin2
  N20: U13.pin3, J2.pin2
  N21: U14.pin3, J2.pin5
  N22: U15.pin3, J2.pin1
  N23: U16.pin3, R4.Pin_1, 10kΩ_3.Pin_1, J5.pin1
  N24: U17.pin3, J3.pin9
  N25: U18.pin3, J5.pin2
  N26: U19.pin3, J3.pin5
  N27: U20.pin3, J2.pin6
  N28: esp-01.pin4, rx_tx_gnd.pin3
  N29: esp-01.pin7, 10kΩ_2.Pin_1
  N30: esp-01.pin8, rx_tx_gnd.pin2

notes:
  03 02 01 00 A6 A7 13 A3
  https://hackaday.io/project/9927-tote-had
